# Fritzing sketch arduino blink two pins (saved by Fritzing 0.5.2b)
breadboards: 1

parts:
  Arduino1 = Arduino
  LED1 = Red LED - 5mm [package="5 mm [THT]"]
  LED2 = Blue LED - 5mm [package="5 mm [THT]"]
  R1 = Resistor [resistance=220 package=THT]
  R2 = Resistor [resistance=220 package=THT]

nets:
  N1: Arduino1.GND, LED1.cathode, LED2.cathode
  N2: Arduino1.D11, R1.Pin_1
  N3: Arduino1.D10, R2.Pin_1
  N4: LED1.anode, R1.Pin_0
  N5: LED2.anode, R2.Pin_0
