# Fritzing sketch basic blink (saved by Fritzing 0.5.2b)
breadboards: 1

parts:
  Arduino1 = Arduino
  LED1 = Red LED - 5mm [package="5 mm [THT]"]
  R1 = Resistor [resistance=220 package=THT]

nets:
  N1: Arduino1.GND, LED1.cathode
  N2: Arduino1.D13, R1.Pin_1
  N3: LED1.anode, R1.Pin_0
