# Fritzing sketch modified forloop (saved by Fritzing 0.5.2b)
breadboards: 1

parts:
  Arduino1 = Arduino
  LED1 = Red LED - 5mm [package="5 mm [THT]"]
  LED2 = Blue LED - 5mm [package="5 mm [THT]"]
  R1 = Resistor [resistance=220 package=THT]
  R2 = Resistor [resistance=220 package=THT]
  LED3 = green LED - 5mm [package="5 mm [THT]"]
  R3 = Resistor [resistance=220 package=THT]
  R4 = Resistor [resistance=220 package=THT]
  R5 = Resistor [resistance=220 package=THT]
  R6 = Resistor [resistance=220 package=THT]
  LED4 = yellow LED - 5mm [package="5 mm [THT]"]
  LED5 = white LED - 5mm [package="5 mm [THT]"]
  LED6 = white LED - 5mm [package="5 mm [THT]"]

nets:
  N1: Arduino1.GND, LED1.cathode, LED2.cathode, LED3.cathode, LED4.cathode, LED5.cathode, LED6.cathode
  N2: Arduino1.D7, R1.Pin_1
  N3: Arduino1.D6, R2.Pin_1
  N4: Arduino1.D5, R3.Pin_1
  N5: Arduino1.D4, R6.Pin_1
  N6: Arduino1.D3, R5.Pin_1
  N7: Arduino1.D2, R4.Pin_1
  N8: LED1.anode, R5.Pin_0
  N9: LED2.anode, R2.Pin_0
  N10: R1.Pin_0, LED6.anode
  N11: LED3.anode, R3.Pin_0
  N12: R4.Pin_0, LED5.anode
  N13: R6.Pin_0, LED4.anode
