# Fritzing sketch pwm_rotary_potentiometer (saved by Fritzing 0.5.2b)
breadboards: 1

parts:
  Arduino1 = Arduino
  LED1 = Red LED - 5mm [package="5 mm [THT]"]
  R1 = Rotary Potentiometer (Small)

nets:
  N1: Arduino1.D9, LED1.anode
  N2: Arduino1.+5V, R1.leg2
  N3: Arduino1.A2, R1.wiper
  N4: LED1.cathode, R1.leg1
