# Fritzing sketch networked_lamp_schematic (saved by Fritzing 0.5.2b)
breadboards: 1

parts:
  Arduino1 = Arduino
  LED1 = Red LED - 5mm [package="5 mm [THT]"]
  LED2 = Red LED - 5mm [package="5 mm [THT]"]
  LED3 = Red LED - 5mm [package="5 mm [THT]"]
  LED4 = Blue LED - 5mm [package="5 mm [THT]"]
  LED5 = Blue LED - 5mm [package="5 mm [THT]"]
  LED6 = Blue LED - 5mm [package="5 mm [THT]"]
  LED7 = green LED - 5mm [package="5 mm [THT]"]
  LED8 = green LED - 5mm [package="5 mm [THT]"]
  LED9 = green LED - 5mm [package="5 mm [THT]"]
  R1 = Rotary Potentiometer (Small)
  R2 = Rotary Potentiometer (Small)
  R3 = Slide Potentiometer
  R4 = Resistor [resistance=330 package=THT]
  R4_2 = Resistor [resistance=330 package=THT]
  R4_3 = Resistor [resistance=330 package=THT]
  R4_4 = Resistor [resistance=330 package=THT]
  R4_5 = Resistor [resistance=330 package=THT]
  R4_6 = Resistor [resistance=330 package=THT]
  R4_7 = Resistor [resistance=330 package=THT]
  R4_8 = Resistor [resistance=330 package=THT]
  R4_9 = Resistor [resistance=330 package=THT]
  S1 = Pushbutton [package=THT]

nets:
  N1: Arduino1.GND, LED1.cathode, LED2.cathode, LED3.cathode, LED4.cathode, LED5.cathode, LED6.cathode, LED7.cathode, LED8.cathode, LED9.cathode, R1.leg2, R2.leg2, R3.leg2
  N2: Arduino1.D11, R4.Pin_0, R4_8.Pin_1, R4_9.Pin_0
  N3: Arduino1.D10, R4_5.Pin_1, R4_6.Pin_0, R4_7.Pin_0
  N4: Arduino1.D9, R4_2.Pin_1, R4_3.Pin_0, R4_4.Pin_0
  N5: Arduino1.+5V, S1.leg0
  N6: Arduino1.A0, R2.wiper
  N7: Arduino1.A2, R1.wiper
  N8: Arduino1.A3, R3.wiper
  N9: LED1.anode, R4_4.Pin_1
  N10: LED2.anode, R4_3.Pin_1
  N11: LED3.anode, R4_2.Pin_0
  N12: LED4.anode, R4.Pin_1
  N13: LED5.anode, R4_9.Pin_1
  N14: LED6.anode, R4_8.Pin_0
  N15: LED7.anode, R4_7.Pin_1
  N16: LED8.anode, R4_6.Pin_1
  N17: LED9.anode, R4_5.Pin_0
  N18: R1.leg1, R2.leg1, R3.leg1, S1.leg1
